// Logisim project logis.circ as structural Verilog: 1 circuit, main circuit main
module main (
  input  A,
  input  B,
  input  B_2,
  input  C,
  output F
);

  wire and_1_out, and_2_out, not_1_out;

  not not_1 (not_1_out, B);
  and and_1 (and_1_out, A, not_1_out);
  and and_2 (and_2_out, B_2, C);
  or or_1 (F, and_1_out, and_2_out);
endmodule
